// Logisim project myAlu.circ as structural Verilog
module myNOT (
  input  in_1,
  output out_2
);

  nand nand_1 (out_2, in_1, in_1);
endmodule

module myAND (
  input  in_1,
  input  in_2,
  output out_3
);

  wire nand_1_out;

  nand nand_1 (nand_1_out, in_1, in_2);
  myNOT mynot_1 (.in_1(nand_1_out), .out_2(out_3));
endmodule

module myOR (
  input  in_1,
  input  in_2,
  output out_3
);

  wire mynot_1_out_2, mynot_2_out_2;

  myNOT mynot_1 (.in_1(in_1), .out_2(mynot_1_out_2));
  myNOT mynot_2 (.in_1(in_2), .out_2(mynot_2_out_2));
  nand nand_1 (out_3, mynot_1_out_2, mynot_2_out_2);
endmodule

module myXOR (
  input  in_1,
  input  in_2,
  output out_3
);

  wire myand_1_out_3, myand_2_out_3, mynot_1_out_2, mynot_2_out_2;

  myNOT mynot_1 (.in_1(in_1), .out_2(mynot_1_out_2));
  myNOT mynot_2 (.in_1(in_2), .out_2(mynot_2_out_2));
  myAND myand_1 (.in_1(mynot_1_out_2), .in_2(in_2), .out_3(myand_1_out_3));
  myAND myand_2 (.in_1(in_1), .in_2(mynot_2_out_2), .out_3(myand_2_out_3));
  myOR myor_1 (.in_1(myand_1_out_3), .in_2(myand_2_out_3), .out_3(out_3));
endmodule

module myMUX (
  input  A,
  input  B,
  input  in_3,
  output out_4
);

  wire myand_1_out_3, myand_2_out_3, mynot_1_out_2;

  myNOT mynot_1 (.in_1(in_3), .out_2(mynot_1_out_2));
  myAND myand_1 (.in_1(A), .in_2(mynot_1_out_2), .out_3(myand_1_out_3));
  myAND myand_2 (.in_1(B), .in_2(in_3), .out_3(myand_2_out_3));
  myXOR myxor_1 (.in_1(myand_1_out_3), .in_2(myand_2_out_3), .out_3(out_4));
endmodule

module myDMUX (
  input  in_1,
  input  in_2,
  output out_3,
  output out_4
);

  wire mynot_1_out_2;

  myNOT mynot_1 (.in_1(in_2), .out_2(mynot_1_out_2));
  myAND myand_1 (.in_1(in_1), .in_2(mynot_1_out_2), .out_3(out_3));
  myAND myand_2 (.in_1(in_1), .in_2(in_2), .out_3(out_4));
endmodule

module myHalfAdder (
  input  in_1,
  input  in_2,
  output S,
  output C
);

  myXOR myxor_1 (.in_1(in_1), .in_2(in_2), .out_3(S));
  myAND myand_1 (.in_1(in_1), .in_2(in_2), .out_3(C));
endmodule

module myFullAdder (
  input  in_1,
  input  A,
  input  B,
  output S,
  output C
);

  wire myhalfadder_1_c, myhalfadder_1_s, myhalfadder_2_c;

  myHalfAdder myhalfadder_1 (.in_1(A), .in_2(B), .S(myhalfadder_1_s), .C(myhalfadder_1_c));
  myHalfAdder myhalfadder_2 (.in_1(in_1), .in_2(myhalfadder_1_s), .S(S), .C(myhalfadder_2_c));
  myOR myor_1 (.in_1(myhalfadder_2_c), .in_2(myhalfadder_1_c), .out_3(C));
endmodule

module myALU (
  input  in_1,
  input  in_2,
  input  in_3,
  input  in_4,
  input  in_5,
  input  in_6,
  input  in_7,
  output out_8
);

  wire myand_1_out_3, myfulladder_1_s, myfulladder_2_s, mymux_2_out_4, mymux_3_out_4, mymux_4_out_4,
       mymux_5_out_4, mynot_1_out_2, myor_1_out_3, myxor_1_out_3;

  myFullAdder myfulladder_1 (.A(in_1), .B(in_2), .S(myfulladder_1_s));  // open: in_1, C
  myFullAdder myfulladder_2 (.A(in_1), .B(in_2), .S(myfulladder_2_s));  // open: in_1, C
  myAND myand_1 (.in_1(in_1), .in_2(in_2), .out_3(myand_1_out_3));
  myOR myor_1 (.in_1(in_1), .in_2(in_2), .out_3(myor_1_out_3));
  myXOR myxor_1 (.in_1(in_1), .in_2(in_2), .out_3(myxor_1_out_3));
  myNOT mynot_1 (.in_1(in_1), .out_2(mynot_1_out_2));
  myMUX mymux_1 (.A(myfulladder_1_s), .B(mymux_5_out_4), .in_3(in_6), .out_4(out_8));
  myMUX mymux_2 (.A(myand_1_out_3), .B(in_4), .in_3(mymux_3_out_4), .out_4(mymux_2_out_4));
  myMUX mymux_3 (.A(myor_1_out_3), .B(mymux_4_out_4), .in_3(in_3), .out_4(mymux_3_out_4));
  myMUX mymux_4 (.A(myxor_1_out_3), .B(mynot_1_out_2), .in_3(in_7), .out_4(mymux_4_out_4));
  myMUX mymux_5 (.A(myfulladder_2_s), .B(mymux_2_out_4), .in_3(in_5), .out_4(mymux_5_out_4));
endmodule

module AU (
  input  Cin,
  input  A,
  input  in_3,
  input  B,
  input  in_5,
  output S,
  output Cout
);

  wire myor_1_out_3, myxor_1_out_3;

  myOR myor_1 (.in_1(B), .in_2(in_5), .out_3(myor_1_out_3));
  myXOR myxor_1 (.in_1(myor_1_out_3), .in_2(in_3), .out_3(myxor_1_out_3));
  myFullAdder myfulladder_1 (.in_1(Cin), .A(A), .B(myxor_1_out_3), .S(S), .C(Cout));
endmodule
